# Fritzing sketch MEGA (saved by Fritzing 1.0.4)

parts:
  Part1 = Arduino Mega 2560 (Rev3)
  Part2 = NRF24L01+ Breakout Board
  U2 = Voltage Regulator [package=to220-adj]
  U3 = LIPO-1000mAh [package=lipo-1000]
  U4 = LIPO-1000mAh [package=lipo-1000]
  U5 = LIPO-1000mAh [package=lipo-1000]
  C3 = Electrolytic Capacitor [capacitance=0.22µF voltage=35V package="1010 [SMD, electrolytic]"]
  C6 = Electrolytic Capacitor [capacitance=100nF voltage=35V package="1010 [SMD, electrolytic]"]
  C7 = Electrolytic Capacitor [capacitance=100µF voltage=35V package="1010 [SMD, electrolytic]"]
  J1 = Basic Servo
  U6 = SWITCH_SPDT [package=kps-1290]
  U7 = Voltage Regulator [package=to220-adj]
  Mod1 = Heltec WiFi LoRa 32 V2 [part_number=HTIT-WB32LA]
  U8 = LIPO-1000mAh [package=lipo-1000]
  Part3 = BME280 Breakout
  U9 = SUP500F [package=sup500f]

nets:
  GND: Part1.GND, Part2.GND, U2.ADJ, U5.-, C3.-, C6.-, C7.-, J1.gnd, U6.O, U7.ADJ
  N1: Part1.D8_PWM, Part2.CS
  N2: Part1.VIN, U6.P, U7.IN
  N3: Part1.D3_PWM, J1.pulse
  N4: Part1.D7_PWM, Part2.CE
  N5: Part1.D50, Part2.MISO
  N6: Part1.D51, Part2.MOSI
  N7: Part1.D52, Part2.SCK
  N8: Part2.VCC, U2.OUT, C7.+
  N9: U2.IN, C6.+, U7.OUT
  N10: U3.+, U6.S
  N11: U3.-, U4.+
  N12: U4.-, U5.+
  N13: Mod1.pin_1, Part3.SDI/SDA
  3.3V: Mod1.pin_16, Mod1.pin_17, Part3.3.3V, U9.VCC
  GND_2: Mod1.GND, U8.-, Part3.GND
  N14: Mod1.pin_21, Mod1.pin_22, U8.+
  N15: Mod1.pin_23, U9.TX-O
  N16: Mod1.pin_24, U9.RX-I
  N17: Mod1.pin_27, Part3.SCK/SCL

notes:
  5V Regulator
  3.3V Regulator
  5-12V VIA Vessel Controls Power System
  PWM Line to ESC
  ON/OFF Switch
  Digital Communication to Servo
  Decoupling Caps
  HelTec V3 LoRa Microcontroller
  BME 280
  Enviromental Sensor
  GT-7U
  GPS
  GPS:
  R:3V3
  B:GND
  P:TX
  C:RX
  Serial UART - TX and RX Wires Swap On Microcontroller
  Blue Wire is a TX line on the ESC Which Goes Into RX Pin on Microcontroller
